# Fritzing sketch Car_Schematic (saved by Fritzing 0.9.3b)
breadboards: 1

parts:
  Part1 = Arduino Uno (Rev3)
  Raspberry_Pi1 = Raspberry Pi B+  # not connected
  L298N2 = L298N DC motor driver
  DC_Mot_Enc1 = DC Motor with two-phase hall-encoder [part_number=VT-E-G25A-06-177E]
  HC-SR04_Sensor_1 = HC-SR04 Ultrasonic Distance Sensor
  HC-SR04_Sensor_2 = HC-SR04 Ultrasonic Distance Sensor
  HC-SR04_Sensor_3 = HC-SR04 Ultrasonic Distance Sensor
  J1 = Basic Servo
  Part3 = InvenSense MPU6050
  VCC1 = Battery block 9V
  U1 = TCM8240MD [package=tcm8240md]  # not connected

nets:
  N1: Part1.A0, HC-SR04_Sensor_2.ECHO
  N2: Part1.A1, HC-SR04_Sensor_3.ECHO
  N3: Part1.A2, HC-SR04_Sensor_1.ECHO
  N4: Part1.A4/SDA, Part3.SDA
  N5: Part1.A5/SCL, Part3.SCL
  N6: Part1.D8, L298N2.IN1
  N7: Part1.D9_PWM, L298N2.IN2
  N8: Part1.D12/MISO, J1.pulse
  N9: Part1.D13/SCK, HC-SR04_Sensor_2.TRIG
  GND: Part1.GND, L298N2.GND, DC_Mot_Enc1.pin2, HC-SR04_Sensor_1.GND, HC-SR04_Sensor_2.GND, HC-SR04_Sensor_3.GND, J1.gnd, Part3.GND
  N10: Part1.D2, DC_Mot_Enc1.pin4
  N11: Part1.D3_PWM, DC_Mot_Enc1.pin3
  N12: Part1.D4, HC-SR04_Sensor_1.TRIG
  N13: Part1.D7, HC-SR04_Sensor_3.TRIG
  VCC: Part1.5V, L298N2.5V, DC_Mot_Enc1.pin5, HC-SR04_Sensor_1.VCC, HC-SR04_Sensor_2.VCC, HC-SR04_Sensor_3.VCC, J1.vcc, Part3.VCC, VCC1.-
  N14: L298N2.OUT1, DC_Mot_Enc1.pin6
  N15: L298N2.OUT2, DC_Mot_Enc1.pin1
  N16: L298N2.12V, VCC1.+

notes:
  1 - Motor +
  2 - Encoder +
  3 - Encoder Phase A
  4 - Encoder Phase B
  5 - Encoder
  6 - Motor -
  1 PI & PI CA
  Raspberry PI & Ca

custom parts:
  L298N DC motor driver: 2x DC motor driver with 78M05 positive voltage regulator (7..35 V) L298N: max 46 V, 2 A Set 5 V Enable jumper to enable 5 V regultor (needed for the L298N) and +5 V output at screw terminal or supply external +5 V at screw terminal Set ENA and/or ENB to +5 V to enable motor permanently or supply ENA and/or ENB with PWM signal IN1 and IN2 set rotation directory for motor A (OUT1/OUT2) IN2 and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

// code stored in the sketch: Untitled.ino

